# Fritzing sketch sensor (saved by Fritzing 0.7.12b)
breadboards: 1

parts:
  Arduino1 = Arduino
  S1 = Basic Force Sensing Resistor (FSR) [part_number="Soil Moisture Sensor" package=THT]
  R1 = Resistor [tolerance=±5% resistance=10k part_number=10k package=THT]

nets:
  N1: Arduino1.GND, R1.Pin_1
  N2: Arduino1.+5V, S1.pin_0
  N3: Arduino1.A0, S1.pin_1, R1.Pin_0
